# Fritzing sketch lagmeter (saved by Fritzing 0.9.4)
breadboards: 1

parts:
  Part1 = Arduino Leonardo (Rev3b)
  R1 = Resistor [tolerance=±5% resistance=220 package="0402 [SMD]"]
  S1 = Momentary Switch [package=ksa_sealed_tac_switch]
  Q1 = LTR-301 [package=ltr-301]
  Grove1 = Grove OLED 128x96

nets:
  N1: Part1.D2/SDA, Grove1.SDA
  N2: Part1.D3_PWM/SCL, Grove1.SCL
  N3: Part1.D7, S1.1, S1.2
  3V3: Part1.3V3, Q1.C, Grove1.VCC
  GND: Part1.GND, R1.Pin_0, S1.3, S1.4, Grove1.GND
  N4: Part1.A0, R1.Pin_1, Q1.E
